# Fritzing sketch ArduinoSpeadMeasure (saved by Fritzing 1.0.1rc)
breadboards: 1

parts:
  Part2 = Arduino Pro Micro (Clone)
  LCD3 = LCD screen
  LCM1602_IIC3 = LCM1602 IIC [part_number="LCM1602 IIC" chip_label="LCM1602 IIC" package="DIP (Dual Inline) [THT]"]
  Enc1 = shaft encoder  # not connected
  Enc2 = shaft encoder  # not connected

nets:
  GND: Part2.GND, LCM1602_IIC3.GND
  N1: Part2.D2, LCM1602_IIC3.SCL
  VCC: Part2.VCC, LCM1602_IIC3.VCC
  VSS: LCD3.VSS, LCM1602_IIC3.VSS
  VDD: LCD3.VDD, LCM1602_IIC3.VDD
  N2: LCD3.V0, LCM1602_IIC3.V0
  N3: LCD3.RS, LCM1602_IIC3.RS
  N4: LCD3.R/W, LCM1602_IIC3.RW
  N5: LCD3.E, LCM1602_IIC3.E
  N6: LCD3.DB0, LCM1602_IIC3.D0
  N7: LCD3.DB1, LCM1602_IIC3.D1
  N8: LCD3.DB2, LCM1602_IIC3.D2
  N9: LCD3.DB3, LCM1602_IIC3.D3
  N10: LCD3.DB4, LCM1602_IIC3.D4
  N11: LCD3.DB5, LCM1602_IIC3.D5
  N12: LCD3.DB6, LCM1602_IIC3.D6
  N13: LCD3.DB7, LCM1602_IIC3.D7
  N14: LCD3.LED+, LCM1602_IIC3.A
  N15: LCD3.LED-, LCM1602_IIC3.K
  N16: LCM1602_IIC3.LED_A, LCM1602_IIC3.LED_B

notes:
  SDA = 2 SLC = 3

custom parts:
  LCM1602 IIC: I2C-Module to use a 1602 or 2004 LCD on with the wire.h libory Serial LCD Modul
